// Logisim project v1.circ as structural Verilog: 1 circuit, main circuit main
module main (
  output [2:0] CPUstep,
  output [15:0] Adress,
  output CPUclk,
  output [15:0] Data,
  output ReadWrite,
  output Strobe,
  output Reset,
  output Interrupt,
  output DMA,
  output CLK,
  output Hold
);

  wire and_1_out, and_2_out, and_3_out, and_4_out, and_5_out, and_6_out, and_7_out, and_8_out, and_9_out,
       and_10_out, and_11_out, and_12_out, and_13_out, and_14_out, and_15_out, and_16_out, and_17_out,
       and_18_out, and_19_out, and_20_out, and_21_out, and_22_out, and_23_out, and_24_out, and_25_out,
       and_26_out, and_28_out, and_29_out, and_30_out, and_31_out, and_32_out, and_33_out, and_34_out,
       and_35_out, and_36_out, and_37_out, and_38_out, and_39_out, and_40_out, and_41_out, and_42_out,
       and_43_out, and_44_out, and_45_out, and_46_out, button_1_out, button_2_out, button_3_out,
       comparator_1_eq, comparator_2_eq, comparator_3_eq, comparator_4_eq, comparator_5_eq, comparator_6_eq,
       comparator_7_eq, comparator_8_eq, comparator_9_eq, comparator_10_eq, comparator_11_eq,
       comparator_12_eq, comparator_13_eq, comparator_14_eq, comparator_14_gt, comparator_14_lt,
       comparator_15_eq, comparator_16_eq, d_ff_1_qn, d_ff_2_q, demultiplexer_1_out0, demultiplexer_1_out1,
       j_k_ff_1_qn, not_1_out, not_2_out, not_3_out, not_4_out, not_7_out, not_8_out, not_9_out, or_1_out,
       or_2_out, or_4_out, or_5_out, or_6_out, or_7_out, or_8_out, or_10_out, or_11_out, or_12_out,
       or_13_out, or_14_out, or_15_out, or_16_out, or_17_out, or_18_out, or_19_out, or_20_out, or_21_out,
       or_22_out, or_23_out, or_24_out, or_25_out, or_26_out, or_27_out, or_28_out, or_29_out, or_30_out,
       or_31_out, or_32_out, or_33_out, or_34_out, or_35_out, or_36_out, or_37_out, or_38_out, or_39_out,
       or_40_out, or_41_out, or_42_out, or_43_out, or_44_out, or_45_out, or_46_out, or_47_out, or_48_out,
       or_49_out, or_50_out, or_51_out, or_52_out, or_53_out, or_54_out, or_55_out, or_56_out, or_57_out,
       or_58_out, or_59_out, or_60_out, or_61_out, or_62_out, or_63_out, or_64_out, or_65_out, por_1_out,
       t_ff_1_q, t_ff_1_qn, xor_1_out;
  wire [3:0] register_8_q, register_8_q_2, register_8_q_3, register_8_q_4;
  wire [6:0] keyboard_1_data, keyboard_2_data;
  wire [15:0] adder_1_out, adder_3_out, adder_4_out, adder_5_out, and_27_out, bit_extender_2_out,
       bit_extender_3_out, bit_extender_4_out, controlled_buffer_12_out, controlled_buffer_19_out,
       counter_1_q, counter_2_q, counter_3_q, multiplexer_1_out, multiplexer_2_out, multiplexer_3_out,
       multiplexer_4_out, negator_1_out, negator_2_out, not_5_out, not_6_out, or_3_out, register_1_q,
       register_2_q, register_3_q, register_4_q, register_5_q, register_6_q, register_7_q, register_9_q,
       register_10_q, rom_1_data, rom_2_data, undriven;
  wire [23:0] adder_2_out, bit_extender_1_out;

  TTY #(.cols(52), .rows(16)) tty_1 (.data(Data[6:0]), .clk(and_4_out), .clr(Reset));  // open: we
  Keyboard #(.buflen(256)) keyboard_1 (
    .clk(and_1_out), .clr(Reset), .avail(Interrupt), .data(keyboard_1_data));  // open: re
  Pull_Resistor pull_resistor_1 (.node(Adress));
  Pull_Resistor pull_resistor_2 (.node(Data));
  Pull_Resistor pull_resistor_3 (.node(ReadWrite));
  Pull_Resistor pull_resistor_4 (.node(Strobe));
  Pull_Resistor pull_resistor_5 (.node(Interrupt));
  Pull_Resistor pull_resistor_6 (.node(DMA));
  Pull_Resistor pull_resistor_7 (.node(CLK));
  Pull_Resistor pull_resistor_8 (.node(Reset));
  and and_1 (and_1_out, comparator_1_eq, ReadWrite, Strobe);
  Comparator #(.mode("unsigned"), .width(16)) comparator_1 (
    .a(16'hfff7), .b(Adress), .eq(comparator_1_eq));  // open: gt, lt
  Pull_Resistor pull_resistor_9 (.node(Hold));
  and and_2 (and_2_out, comparator_1_eq, ~ReadWrite);  // AND_Gate
  assign Data = and_2_out ? {{9{1'b0}}, keyboard_1_data} : 16'bz;  // Controlled_Buffer controlled_buffer_1
  Comparator #(.mode("unsigned"), .width(16)) comparator_2 (
    .a(16'hfff8), .b(Adress), .eq(comparator_2_eq));  // open: gt, lt
  Register #(.width(16)) register_1 (.D(Data), .Q(register_1_q), .clk(and_3_out), .clr(Reset));  // open: en
  and and_3 (and_3_out, comparator_3_eq, ReadWrite, Strobe);
  Comparator #(.mode("unsigned"), .width(16)) comparator_3 (
    .a(16'hfffa), .b(Adress), .eq(comparator_3_eq));  // open: gt, lt
  and and_4 (and_4_out, comparator_2_eq, ReadWrite, Strobe);
  and and_5 (and_5_out, comparator_3_eq, ~ReadWrite);  // AND_Gate
  assign Data = and_5_out ? register_1_q : 16'bz;  // Controlled_Buffer controlled_buffer_2
  Comparator #(.mode("unsigned"), .width(16)) comparator_4 (
    .a(16'hfff2), .b(Adress), .eq(comparator_4_eq));  // open: gt, lt
  and and_6 (and_6_out, comparator_5_eq, ~ReadWrite);  // AND_Gate
  Comparator #(.mode("unsigned"), .width(16)) comparator_5 (
    .a(16'hfff3), .b(Adress), .eq(comparator_5_eq));  // open: gt, lt
  and and_7 (and_7_out, comparator_6_eq, ~ReadWrite);  // AND_Gate
  Comparator #(.mode("unsigned"), .width(16)) comparator_6 (
    .a(16'hfff4), .b(Adress), .eq(comparator_6_eq));  // open: gt, lt
  and and_8 (and_8_out, comparator_7_eq, ~ReadWrite);  // AND_Gate
  Comparator #(.mode("unsigned"), .width(16)) comparator_7 (
    .a(16'hfff5), .b(Adress), .eq(comparator_7_eq));  // open: gt, lt
  and and_9 (and_9_out, comparator_8_eq, ~ReadWrite);  // AND_Gate
  Comparator #(.mode("unsigned"), .width(16)) comparator_8 (
    .a(16'hfff6), .b(Adress), .eq(comparator_8_eq));  // open: gt, lt
  ROM #(.dataWidth(16)) rom_1 (.addr(Adress[7:0]), .data(rom_1_data));
  and and_10 (and_10_out, d_ff_1_qn, DMA);
  and and_11 (and_11_out, comparator_9_eq, ReadWrite, Strobe);
  Comparator #(.mode("unsigned"), .width(16)) comparator_9 (
    .a(16'hfffb), .b(Adress), .eq(comparator_9_eq));  // open: gt, lt
  and and_12 (and_12_out, comparator_4_eq, ReadWrite, Strobe);
  or or_1 (or_1_out, and_12_out, Reset);
  assign Data = and_6_out ? register_2_q : 16'bz;  // Controlled_Buffer controlled_buffer_3
  Register #(.width(16)) register_2 (.D(Data), .Q(register_2_q), .clk(and_13_out), .clr(Reset));  // open: en
  and and_13 (and_13_out, comparator_5_eq, ReadWrite, Strobe);
  assign Data = and_7_out ? register_3_q : 16'bz;  // Controlled_Buffer controlled_buffer_4
  Register #(.width(16)) register_3 (.D(Data), .Q(register_3_q), .clk(and_14_out), .clr(Reset));  // open: en
  and and_14 (and_14_out, comparator_6_eq, ReadWrite, Strobe);
  assign Data = and_8_out ? register_4_q : 16'bz;  // Controlled_Buffer controlled_buffer_5
  Register #(.width(16)) register_4 (.D(Data), .Q(register_4_q), .clk(and_15_out), .clr(Reset));  // open: en
  and and_15 (and_15_out, comparator_7_eq, ReadWrite, Strobe);
  assign Data = and_9_out ? register_5_q : 16'bz;  // Controlled_Buffer controlled_buffer_6
  Register #(.width(16)) register_5 (.D(Data), .Q(register_5_q), .clk(and_16_out), .clr(Reset));  // open: en
  and and_16 (and_16_out, comparator_8_eq, ReadWrite, Strobe);
  D_Flip_Flop d_ff_1 (.clk(and_10_out), .D(and_10_out), .Qn(d_ff_1_qn), .reset(Reset));  // open: Q, preset
  and and_17 (and_17_out, and_18_out, Strobe);
  not not_1 (not_1_out, Adress[15]);
  and and_18 (and_18_out, not_1_out, ~d_ff_1_qn);  // AND_Gate
  Negator #(.width(16)) negator_1 (.in(register_6_q), .out(negator_1_out));
  Register #(.width(16)) register_6 (.D(Data), .Q(register_6_q), .clk(and_11_out), .clr(Reset));  // open: en
  and and_19 (and_19_out, comparator_9_eq, ~ReadWrite);  // AND_Gate
  assign Data = and_19_out ? register_6_q : 16'bz;  // Controlled_Buffer controlled_buffer_7
  assign Adress = DMA ? adder_1_out : 16'bz;  // Controlled_Buffer controlled_buffer_8
  assign Data = DMA ? rom_2_data : 16'bz;  // Controlled_Buffer controlled_buffer_9
  assign ReadWrite = DMA ? 1'b1 : 1'bz;  // Controlled_Buffer controlled_buffer_10
  assign Strobe = DMA ? t_ff_1_q : 1'bz;  // Controlled_Buffer controlled_buffer_11
  not not_2 (not_2_out, ReadWrite);
  assign controlled_buffer_12_out = ReadWrite ? Data : 16'bz;  // Controlled_Buffer controlled_buffer_12
  and and_20 (and_20_out, and_18_out, ~ReadWrite);  // AND_Gate
  assign Data = and_20_out ? controlled_buffer_12_out : 16'bz;  // Controlled_Buffer controlled_buffer_13
  assign Data = and_21_out ? rom_1_data : 16'bz;  // Controlled_Buffer controlled_buffer_14
  not not_3 (not_3_out, register_1_q[3]);
  Multiplexer #(.enable("false"), .width(16)) multiplexer_1 (
    .in0(negator_1_out), .in1(register_6_q), .out(multiplexer_1_out), .sel(not_3_out));
  Comparator #(.mode("unsigned"), .width(16)) comparator_10 (
    .a(16'hfffc), .b(Adress), .eq(comparator_10_eq));  // open: gt, lt
  J_K_Flip_Flop j_k_ff_1 (
    .J(or_1_out), .clk(or_2_out), .K(comparator_11_eq), .Q(DMA), .Qn(j_k_ff_1_qn), .reset(Reset));  // open: preset
  or or_2 (or_2_out, or_1_out, comparator_11_eq);
  Counter #(.max('hffff), .width(16)) counter_1 (
    .Q(counter_1_q), .clk(t_ff_1_qn), .clr(j_k_ff_1_qn));  // open: load, D, count, carry, up
  Adder #(.width(16)) adder_1 (.a(register_2_q), .b(counter_1_q), .out(adder_1_out));  // open: cin, cout
  assign bit_extender_1_out = {{8{counter_1_q[15]}}, counter_1_q};  // Bit_Extender bit_extender_1
  Adder #(.width(24)) adder_2 (
    .a(bit_extender_1_out), .b({register_5_q[7:0], register_4_q}), .out(adder_2_out));  // open: cin, cout
  RAM #(.addrWidth(16), .asyncread("true"), .clearpin("true"), .dataWidth(16), .databus("bidir")) ram_1 (
    .addr(Adress), .we(and_18_out), .oe(not_2_out), .clk(and_17_out), .data(controlled_buffer_12_out),
    .clr(Reset));
  and and_21 (and_21_out, d_ff_1_qn, not_1_out, not_2_out);
  Register #(.width(16)) register_7 (.D(Data), .Q(register_7_q), .clk(and_22_out), .clr(Reset));  // open: en
  and and_22 (and_22_out, comparator_10_eq, ReadWrite, Strobe);
  and and_23 (and_23_out, comparator_10_eq, ~ReadWrite);  // AND_Gate
  T_Flip_Flop t_ff_1 (.clk(CLK), .T(DMA), .Q(t_ff_1_q), .Qn(t_ff_1_qn), .reset(Reset));  // open: preset
  Comparator #(.width(16)) comparator_11 (.a(register_3_q), .b(counter_1_q), .eq(comparator_11_eq));  // open: gt, lt
  Hex_Digit_Display hex_digit_display_1 (.value(register_8_q_4));  // open: dp
  Comparator #(.mode("unsigned"), .width(16)) comparator_12 (
    .a(16'hfff9), .b(Adress), .eq(comparator_12_eq));  // open: gt, lt
  not not_4 (not_4_out, register_1_q[5]);
  Negator #(.width(16)) negator_2 (.in(register_7_q), .out(negator_2_out));
  Multiplexer #(.enable("false"), .width(16)) multiplexer_2 (
    .in0(negator_2_out), .in1(register_7_q), .out(multiplexer_2_out), .sel(not_4_out));
  Comparator #(.mode("unsigned"), .width(16)) comparator_13 (
    .a(16'hfffd), .b(Adress), .eq(comparator_13_eq));  // open: gt, lt
  assign Data = and_23_out ? register_7_q : 16'bz;  // Controlled_Buffer controlled_buffer_15
  Hex_Digit_Display hex_digit_display_2 (.value(register_8_q_3));  // open: dp
  Hex_Digit_Display hex_digit_display_3 (.value(register_8_q_2));  // open: dp
  Register #(.width(16)) register_8 (
    .D(Data), .Q({register_8_q_4, register_8_q_3, register_8_q_2, register_8_q}), .clk(and_24_out),
    .clr(Reset));  // open: en
  and and_24 (and_24_out, comparator_12_eq, ReadWrite, Strobe);
  and and_25 (and_25_out, comparator_13_eq, ~ReadWrite);  // AND_Gate
  assign Data = and_25_out ? multiplexer_3_out : 16'bz;  // Controlled_Buffer controlled_buffer_16
  ROM #(.addrWidth(24), .dataWidth(16)) rom_2 (.addr(adder_2_out), .data(rom_2_data));
  Hex_Digit_Display hex_digit_display_4 (.value(register_8_q));  // open: dp
  and and_26 (and_26_out, comparator_12_eq, ~ReadWrite);  // AND_Gate
  assign Data = and_26_out ? {register_8_q_4, register_8_q_3, register_8_q_2, register_8_q} : 16'bz;  // Controlled_Buffer controlled_buffer_17
  Comparator #(.width(16)) comparator_14 (
    .a(multiplexer_1_out), .b(multiplexer_2_out), .gt(comparator_14_gt), .eq(comparator_14_eq),
    .lt(comparator_14_lt));
  Comparator #(.mode("unsigned"), .width(16)) comparator_15 (
    .a(Adress), .b({16{1'b1}}), .eq(comparator_15_eq));  // open: gt, lt
  Comparator #(.mode("unsigned"), .width(16)) comparator_16 (
    .a(Adress), .b(16'hfffe), .eq(comparator_16_eq));  // open: gt, lt
  Adder #(.width(16)) adder_3 (.a(multiplexer_1_out), .b(multiplexer_2_out), .out(adder_3_out));  // open: cin, cout
  assign bit_extender_2_out = {{15{1'b0}}, comparator_14_gt};  // Bit_Extender bit_extender_2
  assign bit_extender_3_out = {{15{1'b0}}, comparator_14_eq};  // Bit_Extender bit_extender_3
  assign bit_extender_4_out = {{15{1'b0}}, comparator_14_lt};  // Bit_Extender bit_extender_4
  assign and_27_out = multiplexer_1_out & multiplexer_2_out;  // AND_Gate and_27, 16 bits wide
  assign or_3_out = multiplexer_1_out | multiplexer_2_out;  // OR_Gate or_3, 16 bits wide
  assign not_5_out = ~multiplexer_1_out;  // NOT_Gate not_5, 16 bits wide
  Demultiplexer #(.enable("false")) demultiplexer_1 (
    .out0(demultiplexer_1_out0), .out1(demultiplexer_1_out1), .in(or_6_out), .sel(xor_1_out));
  or or_4 (or_4_out, comparator_15_eq, comparator_16_eq);
  and and_28 (and_28_out, or_4_out, ReadWrite);
  and and_29 (and_29_out, or_4_out, ~ReadWrite);  // AND_Gate
  Multiplexer #(.enable("false"), .select(3), .width(16)) multiplexer_3 (
    .in0(adder_3_out), .in1(bit_extender_2_out), .in2(bit_extender_3_out), .in3(bit_extender_4_out),
    .in4(and_27_out), .in5(or_3_out), .in6(not_5_out), .in7(undriven), .out(multiplexer_3_out),
    .sel(register_1_q[2:0]));
  assign not_6_out = ~16'hfe;  // NOT_Gate not_6, 16 bits wide
  Adder #(.width(16)) adder_4 (.a(not_6_out), .b(Data), .out(adder_4_out), .cin(1'b1));  // open: cout
  Counter #(.max('hffff), .width(16)) counter_2 (
    .load(and_28_out), .D(adder_4_out), .count(not_7_out), .Q(counter_2_q), .clk(demultiplexer_1_out1),
    .clr(or_5_out));  // open: carry, up
  Counter #(.max('hffff), .width(16)) counter_3 (
    .load(and_28_out), .D(Data), .count(not_7_out), .Q(counter_3_q), .clk(demultiplexer_1_out0), .clr(Reset));  // open: carry, up
  assign Data = and_29_out ? multiplexer_4_out : 16'bz;  // Controlled_Buffer controlled_buffer_18
  not not_7 (not_7_out, and_28_out);
  and and_30 (and_30_out, and_28_out, Strobe);
  Adder #(.width(16)) adder_5 (.a(16'hfe), .b(counter_2_q), .out(adder_5_out));  // open: cin, cout
  or or_5 (or_5_out, ~d_ff_2_q, Reset);  // OR_Gate
  Multiplexer #(.enable("false"), .width(16)) multiplexer_4 (
    .in0(counter_3_q), .in1(adder_5_out), .out(multiplexer_4_out), .sel(xor_1_out));
  xor xor_1 (xor_1_out, d_ff_2_q, and_32_out);
  or or_6 (or_6_out, and_30_out, and_31_out);
  and and_31 (and_31_out, or_63_out, CPUclk);
  assign controlled_buffer_19_out = or_65_out ? multiplexer_4_out : 16'bz;  // Controlled_Buffer controlled_buffer_19
  and and_32 (and_32_out, comparator_16_eq, ~or_65_out, not_8_out);  // AND_Gate
  assign Adress = not_8_out ? register_9_q : 16'bz;  // Controlled_Buffer controlled_buffer_20
  assign ReadWrite = not_8_out ? or_59_out : 1'bz;  // Controlled_Buffer controlled_buffer_21
  assign Strobe = not_8_out ? and_35_out : 1'bz;  // Controlled_Buffer controlled_buffer_22
  not not_8 (not_8_out, DMA);
  assign controlled_buffer_19_out = or_61_out ? Data : 16'bz;  // Controlled_Buffer controlled_buffer_23
  assign Data = and_34_out ? controlled_buffer_19_out : 16'bz;  // Controlled_Buffer controlled_buffer_24
  and and_33 (and_33_out, ~Hold, or_7_out);  // AND_Gate
  Clock clock_1 (.out(CLK));
  and and_34 (and_34_out, not_8_out, or_59_out);
  and and_35 (and_35_out, or_59_out, CPUclk);
  or or_7 (or_7_out, not_8_out, CPUclk);
  T_Flip_Flop t_ff_2 (.clk(CLK), .T(and_33_out), .Q(CPUclk), .reset(Reset));  // open: Qn, preset
  and and_36 (and_36_out, or_57_out, CPUclk);
  Register #(.width(16)) register_9 (
    .D(controlled_buffer_19_out), .Q(register_9_q), .clk(and_36_out), .clr(Reset));  // open: en
  Register #(.width(16)) register_10 (
    .D(controlled_buffer_19_out), .Q(register_10_q), .clk(and_37_out), .clr(Reset));  // open: en
  and and_37 (and_37_out, or_55_out, CPUclk);
  assign controlled_buffer_19_out = or_53_out ? register_10_q : 16'bz;  // Controlled_Buffer controlled_buffer_25
  Counter #(.max('h7), .width(3)) counter_4 (
    .Q(CPUstep), .clk(not_9_out), .clr(or_8_out));  // open: load, D, count, carry, up
  or or_8 (or_8_out, and_46_out, Reset);
  not not_9 (not_9_out, CPUclk);
  POR por_1 (.out(por_1_out));
  and and_38 (and_38_out, ~CPUstep[0], ~CPUstep[1], ~CPUstep[2]);  // AND_Gate
  or or_9 (Reset, por_1_out, button_1_out);
  Button button_1 (.out(button_1_out));
  buf or_10 (or_10_out, 1'b0);  // OR_Gate
  buf or_11 (or_11_out, 1'b0);  // OR_Gate
  buf or_12 (or_12_out, 1'b0);  // OR_Gate
  or or_13 (or_13_out, and_38_out, 1'b0);
  buf or_14 (or_14_out, 1'b0);  // OR_Gate
  buf or_15 (or_15_out, 1'b0);  // OR_Gate
  buf or_16 (or_16_out, 1'b0);  // OR_Gate
  or or_17 (or_17_out, and_38_out, 1'b0);
  and and_39 (and_39_out, CPUstep[0], ~CPUstep[1], ~CPUstep[2]);  // AND_Gate
  buf or_18 (or_18_out, or_10_out);  // OR_Gate
  buf or_19 (or_19_out, or_18_out);  // OR_Gate
  buf or_20 (or_20_out, or_11_out);  // OR_Gate
  buf or_21 (or_21_out, or_20_out);  // OR_Gate
  buf or_22 (or_22_out, or_12_out);  // OR_Gate
  or or_23 (or_23_out, and_40_out, or_22_out);
  or or_24 (or_24_out, and_39_out, or_13_out);
  buf or_25 (or_25_out, or_24_out);  // OR_Gate
  buf or_26 (or_26_out, or_14_out);  // OR_Gate
  buf or_27 (or_27_out, or_26_out);  // OR_Gate
  or or_28 (or_28_out, and_39_out, or_15_out);
  or or_29 (or_29_out, and_40_out, or_28_out);
  or or_30 (or_30_out, and_39_out, or_16_out);
  buf or_31 (or_31_out, or_30_out);  // OR_Gate
  buf or_32 (or_32_out, or_17_out);  // OR_Gate
  buf or_33 (or_33_out, or_32_out);  // OR_Gate
  and and_40 (and_40_out, ~CPUstep[0], CPUstep[1], ~CPUstep[2]);  // AND_Gate
  and and_41 (and_41_out, or_51_out, CPUclk);
  D_Flip_Flop d_ff_2 (.clk(and_41_out), .D(Interrupt), .Q(d_ff_2_q), .reset(Reset));  // open: Qn, preset
  buf or_34 (or_34_out, or_19_out);  // OR_Gate
  buf or_35 (or_35_out, or_21_out);  // OR_Gate
  buf or_36 (or_36_out, or_23_out);  // OR_Gate
  or or_37 (or_37_out, and_42_out, or_25_out);
  buf or_38 (or_38_out, or_27_out);  // OR_Gate
  buf or_39 (or_39_out, or_29_out);  // OR_Gate
  buf or_40 (or_40_out, or_31_out);  // OR_Gate
  or or_41 (or_41_out, and_42_out, or_33_out);
  and and_42 (and_42_out, CPUstep[0], CPUstep[1], ~CPUstep[2]);  // AND_Gate
  and and_43 (and_43_out, ~CPUstep[0], ~CPUstep[1], CPUstep[2]);  // AND_Gate
  buf or_42 (or_42_out, or_34_out);  // OR_Gate
  buf or_43 (or_43_out, or_35_out);  // OR_Gate
  buf or_44 (or_44_out, or_36_out);  // OR_Gate
  or or_45 (or_45_out, and_43_out, or_37_out);
  buf or_46 (or_46_out, or_38_out);  // OR_Gate
  or or_47 (or_47_out, and_43_out, or_39_out);
  or or_48 (or_48_out, and_43_out, or_40_out);
  buf or_49 (or_49_out, or_41_out);  // OR_Gate
  and and_44 (and_44_out, CPUstep[0], ~CPUstep[1], CPUstep[2]);  // AND_Gate
  buf or_50 (or_50_out, or_42_out);  // OR_Gate
  or or_51 (or_51_out, and_45_out, or_50_out);
  or or_52 (or_52_out, and_44_out, or_43_out);
  buf or_53 (or_53_out, or_52_out);  // OR_Gate
  buf or_54 (or_54_out, or_44_out);  // OR_Gate
  buf or_55 (or_55_out, or_54_out);  // OR_Gate
  buf or_56 (or_56_out, or_45_out);  // OR_Gate
  buf or_57 (or_57_out, or_56_out);  // OR_Gate
  or or_58 (or_58_out, and_44_out, or_46_out);
  buf or_59 (or_59_out, or_58_out);  // OR_Gate
  buf or_60 (or_60_out, or_47_out);  // OR_Gate
  buf or_61 (or_61_out, or_60_out);  // OR_Gate
  buf or_62 (or_62_out, or_48_out);  // OR_Gate
  buf or_63 (or_63_out, or_62_out);  // OR_Gate
  buf or_64 (or_64_out, or_49_out);  // OR_Gate
  buf or_65 (or_65_out, or_64_out);  // OR_Gate
  and and_45 (and_45_out, ~CPUstep[0], CPUstep[1], CPUstep[2]);  // AND_Gate
  Button button_2 (.out(button_2_out));
  Keyboard keyboard_2 (.clk(button_2_out), .clr(button_3_out), .data(keyboard_2_data));  // open: re, avail
  Button button_3 (.out(button_3_out));
  and and_46 (and_46_out, CPUstep[0], CPUstep[1], CPUstep[2]);

  // Notes on the sheet:
  //   contents of rom_1 (hex, n*v repeats v):
  //   b2 ffff 90 90 90 fff2 90 fff7 b4 ffff 91 fff9 9f fff8 a3 fff8 a7 fff8 a2 fff8 aa fff8 a8 fff8 a3
  //   fff8 94 fff8 ae fff8 aa fff8 94 fff8 9a fff8 9d fff8 9b fff8 9e fff8 99 fff8 94 fff8 9c fff8 9e fff8
  //   94 fff8 98 fff8 96 fff8 97 fff8 93 fff8 9d fff8 af fff8 a9 fff8 94 fff8 95 fff8 ab fff8 a7 fff8 a6
  //   fff8 ad fff8 ae fff8 95 fff8 94 fff8 a4 fff8 aa fff8 ac fff8 94 fff8 a0 fff8 b0 fff8 a0 fff8 a6 fff8
  //   a7 fff8 a0 fff8 a1 fff8 a7 fff8 a3 fff8 94 fff8 ab fff8 ac fff8 aa fff8 a5 fff8 ac fff8 a0 fff8 a8
  //   fff8 ad fff8 93 fff8 93 fff8 b1 fff5 90 fff6 b1 fff4 90 fff3 92 fff9 b3 ffff 0 1 3 a 20 22 2e 30 33
  //   43 45 49 4f 52 53 57 61 62 63 65 66 67 69 6c 6d 6e 6f 70 72 73 74 75 76 100 a 4 6 73*0 b4 ffff
  //   Write
  //   Start
  //   Trans
  //   Length
  //   Read
  //   Low
  //   Read
  //   High
  //   0-Uninitialized
  //   1-Working
  //   2-Idle
  //   3-Loading Program
  //   4-Loading Data
  //   5-Halted
  //   contents of rom_2 (hex, n*v repeats v):
  //   73 68 65 6c 6c 0 70 6c 69 73 74 245*0 dc fff2 e8 ffff dc fff2 ea ffff dd fff9 dc fff5 dc fff6 e4
  //   fff4 e5 fff3 e0 fff9 dc fff2 dd fff9 e6 eb e3 fff8 dd ec de fff9 ed ffff dd fff9 e4 ef e4 f0 f2 f3
  //   f4 f5 dc fffa dd fffc f0 fffb fffd f0 e6 f6 f0 38 0 fffb f6 3c 0 fffc de fffa f7 51 fffd fffb dc
  //   fffa e1 fffc fffd fffb ffff fffc fffd 4e dc ffff 52 dc f8 ffff f0 56 0 fffb dc fffc de fffa f5 6d
  //   fffd fffb dc fffa e1 fffc fffd fffb ffff fffc fffd 6a dc ffff 6e dc dc fffa dd fffc f0 fffb fffd f0
  //   f6 fffb fffd f6 f3 ffff f1 f5 f7 f3 dc fffa e4 fffc ef fffb fffd ef f3 ffff ef fff5 dc fff6 e4 fff4
  //   dc fff3 df fff9 e9 ffff fa a7 ec fffb dc fffa e1 fffc fffd fffb ffff fffc fffd a4 dc ffff a8 dc dc
  //   fff7 fb ffff fff7 fffb e2 fffc de fffa fc c3 fffd fffb dc fffa e1 fffc fffd fffb ffff fffc fffd c0
  //   dc ffff c4 dc eb c7 fff7 0 dc fffa eb fffb dd fffc fffd eb fff7 fff8 dc fff7 fa ffff dc ec ee ed fb
  //   ffff 0 1 2 3 4 5 a 3e 100 101 201 0 0 4 8 0 0 20 22 0 0 28 36 0 8a 0 0 54 7c 96 ac a8 d6 0 f9 ffff
  //   a4 fff2 be ffff a4 fff2 c0 ffff a5 fff9 aa fff8 aa fff8 a4 fff5 a4 fff6 bb fff4 bb fff3 a8 fff9 a4
  //   fff2 a5 fff9 ad fff8 b9 fff8 ae fff8 b2 fff8 b3 fff8 ae fff8 af fff8 b3 fff8 b0 fff8 ab fff8 b6 fff8
  //   b7 fff8 b5 fff8 b1 fff8 b7 fff8 ae fff8 b4 fff8 b8 fff8 ac fff8 aa fff8 ba c2 c2 fffb a5 fffc a4
  //   fffa fffd c2 c2 50 0 fffb a4 fffc a6 fffa c4 67 fffd fffb a4 fffa a9 fffc fffd fffb ffff fffc fffd
  //   64 a4 ffff 68 a4 c2 6a 0 fff8 c3 ffff aa fff8 c2 fffb a5 fffc a4 fffa fffd 78 0 fffb a4 fffc a6 fffa
  //   c5 8f fffd fffb a4 fffa a9 fffc fffd fffb ffff fffc fffd 8c a4 ffff 90 a4 c3 ffff aa fff8 bb fff5 a4
  //   fff6 bb fff4 a4 fff3 a7 fff9 bf ffff a4 fff7 c6 ffff 0 1 2 3 4 5 a 20 3a 41 61 62 65 67 69 6c 6d 6f
  //   70 72 73 76 ff 100 0 0 0 4 8 0 0 46 6e 92 a0 55*0 c6 ffff
endmodule
