// Logisim project v2.circ as structural Verilog: 1 circuit, main circuit main
module main (
  output [15:0] Adress,
  output [15:0] Data,
  output ReadWrite,
  output Strobe,
  output Reset,
  output Interrupt,
  output DMA,
  output CLK,
  output InInt,
  output [2:0] CPUstep,
  output CPUclk
);

  wire and_1_out, and_2_out, and_3_out, and_4_out, and_5_out, and_6_out, and_7_out, and_8_out, and_9_out,
       and_10_out, and_11_out, and_12_out, and_13_out, and_14_out, and_15_out, and_16_out, and_17_out,
       and_18_out, and_19_out, and_20_out, and_21_out, and_22_out, and_23_out, and_24_out, and_25_out,
       and_26_out, and_27_out, and_28_out, and_29_out, and_30_out, and_31_out, and_32_out, and_33_out,
       and_34_out, and_35_out, and_37_out, and_38_out, and_39_out, and_40_out, and_41_out, and_42_out,
       and_43_out, and_44_out, and_45_out, and_46_out, and_47_out, and_48_out, and_49_out, and_50_out,
       and_51_out, and_52_out, and_53_out, button_1_out, comparator_1_eq, comparator_2_eq, comparator_3_eq,
       comparator_4_eq, comparator_5_eq, comparator_6_eq, comparator_7_eq, comparator_8_eq, comparator_9_eq,
       comparator_10_eq, comparator_11_eq, comparator_12_eq, comparator_12_gt, comparator_13_eq,
       comparator_14_eq, comparator_15_eq, comparator_16_eq, comparator_17_eq, comparator_18_eq,
       comparator_19_eq, comparator_20_eq, comparator_20_gt, comparator_20_lt, comparator_21_eq,
       comparator_22_eq, d_ff_1_qn, d_ff_2_q, demultiplexer_1_out0, demultiplexer_1_out1,
       demultiplexer_2_out0, demultiplexer_2_out1, j_k_ff_1_qn, multiplexer_2_out, nand_1_out, not_1_out,
       not_2_out, not_3_out, not_4_out, not_5_out, not_6_out, not_7_out, not_8_out, not_11_out, not_12_out,
       not_13_out, or_1_out, or_2_out, or_5_out, or_6_out, or_7_out, or_8_out, or_9_out, or_10_out,
       or_11_out, or_12_out, or_14_out, or_15_out, or_16_out, or_17_out, or_19_out, or_20_out, or_21_out,
       or_22_out, or_23_out, or_24_out, or_25_out, por_1_out, pull_resistor_3_node, pull_resistor_4_node,
       t_ff_1_q, t_ff_1_qn, t_ff_2_q, t_ff_3_q;
  wire [6:0] keyboard_1_data, pull_resistor_2_node;
  wire [7:0] pull_resistor_1_node;
  wire [15:0] adder_1_out, adder_3_out, adder_4_out, adder_5_out, adder_6_out, and_36_out,
       bit_extender_2_out, bit_extender_3_out, bit_extender_4_out, controlled_buffer_10_out,
       controlled_buffer_16_out, controlled_buffer_23_out, controlled_buffer_33_out, counter_1_q,
       counter_2_q, counter_3_q, multiplexer_1_out, multiplexer_3_out, multiplexer_4_out, multiplexer_5_out,
       multiplexer_6_out, negator_1_out, negator_2_out, not_9_out, not_10_out, or_13_out, register_1_q,
       register_2_q, register_3_q, register_4_q, register_5_q, register_6_q, register_7_q, register_8_q,
       register_9_q, register_10_q, register_12_q, register_13_q, rom_1_data, rom_2_data, StatusLCD, undriven;
  wire [15:7] pull_resistor_2_node_2;
  wire [15:8] pull_resistor_1_node_2;
  wire [23:0] adder_2_out, bit_extender_1_out;

  TTY #(.cols(52), .rows(16)) tty_1 (.data(pull_resistor_2_node), .clk(and_3_out), .clr(Reset));  // open: we
  Keyboard #(.buflen(256)) keyboard_1 (
    .clk(and_1_out), .clr(Reset), .avail(Interrupt), .data(keyboard_1_data));  // open: re
  Pull_Resistor pull_resistor_1 (.node({pull_resistor_1_node_2, pull_resistor_1_node}));
  Pull_Resistor pull_resistor_2 (.node({pull_resistor_2_node_2, pull_resistor_2_node}));
  Pull_Resistor pull_resistor_3 (.node(pull_resistor_3_node));
  Pull_Resistor pull_resistor_4 (.node(pull_resistor_4_node));
  Pull_Resistor pull_resistor_5 (.node(Interrupt));
  Pull_Resistor pull_resistor_6 (.node(DMA));
  Pull_Resistor pull_resistor_7 (.node(CLK));
  Pull_Resistor pull_resistor_8 (.node(Reset));
  and and_1 (and_1_out, comparator_1_eq, pull_resistor_3_node, pull_resistor_4_node);
  Comparator #(.mode("unsigned"), .width(16)) comparator_1 (
    .a(16'hfff7), .b({pull_resistor_1_node_2, pull_resistor_1_node}), .eq(comparator_1_eq));  // open: gt, lt
  Pull_Resistor pull_resistor_9 (.node(InInt));
  and and_2 (and_2_out, comparator_1_eq, ~pull_resistor_3_node);  // AND_Gate
  assign {pull_resistor_2_node_2, pull_resistor_2_node} = and_2_out ? {{9{1'b0}}, keyboard_1_data} : 16'bz;  // Controlled_Buffer controlled_buffer_1
  Comparator #(.mode("unsigned"), .width(16)) comparator_2 (
    .a(16'hfff8), .b({pull_resistor_1_node_2, pull_resistor_1_node}), .eq(comparator_2_eq));  // open: gt, lt
  Hex_Digit_Display hex_digit_display_1 (.value(StatusLCD[15:12]));  // open: dp
  and and_3 (and_3_out, comparator_2_eq, pull_resistor_3_node, pull_resistor_4_node);
  Comparator #(.mode("unsigned"), .width(16)) comparator_3 (
    .a(16'hfff2), .b({pull_resistor_1_node_2, pull_resistor_1_node}), .eq(comparator_3_eq));  // open: gt, lt
  and and_4 (and_4_out, comparator_4_eq, ~pull_resistor_3_node);  // AND_Gate
  Comparator #(.mode("unsigned"), .width(16)) comparator_4 (
    .a(16'hfff3), .b({pull_resistor_1_node_2, pull_resistor_1_node}), .eq(comparator_4_eq));  // open: gt, lt
  and and_5 (and_5_out, comparator_5_eq, ~pull_resistor_3_node);  // AND_Gate
  Comparator #(.mode("unsigned"), .width(16)) comparator_5 (
    .a(16'hfff4), .b({pull_resistor_1_node_2, pull_resistor_1_node}), .eq(comparator_5_eq));  // open: gt, lt
  and and_6 (and_6_out, comparator_6_eq, ~pull_resistor_3_node);  // AND_Gate
  Comparator #(.mode("unsigned"), .width(16)) comparator_6 (
    .a(16'hfff5), .b({pull_resistor_1_node_2, pull_resistor_1_node}), .eq(comparator_6_eq));  // open: gt, lt
  and and_7 (and_7_out, comparator_7_eq, ~pull_resistor_3_node);  // AND_Gate
  Comparator #(.mode("unsigned"), .width(16)) comparator_7 (
    .a(16'hfff6), .b({pull_resistor_1_node_2, pull_resistor_1_node}), .eq(comparator_7_eq));  // open: gt, lt
  Hex_Digit_Display hex_digit_display_2 (.value(StatusLCD[11:8]));  // open: dp
  Hex_Digit_Display hex_digit_display_3 (.value(StatusLCD[7:4]));  // open: dp
  and and_8 (and_8_out, comparator_3_eq, pull_resistor_3_node, pull_resistor_4_node);
  or or_1 (or_1_out, and_8_out, Reset);
  assign {pull_resistor_2_node_2, pull_resistor_2_node} = and_4_out ? register_1_q : 16'bz;  // Controlled_Buffer controlled_buffer_2
  Register #(.width(16)) register_1 (
    .D({pull_resistor_2_node_2, pull_resistor_2_node}), .Q(register_1_q), .clk(and_9_out), .clr(Reset));  // open: en
  and and_9 (and_9_out, comparator_4_eq, pull_resistor_3_node, pull_resistor_4_node);
  assign {pull_resistor_2_node_2, pull_resistor_2_node} = and_5_out ? register_2_q : 16'bz;  // Controlled_Buffer controlled_buffer_3
  Register #(.width(16)) register_2 (
    .D({pull_resistor_2_node_2, pull_resistor_2_node}), .Q(register_2_q), .clk(and_10_out), .clr(Reset));  // open: en
  and and_10 (and_10_out, comparator_5_eq, pull_resistor_3_node, pull_resistor_4_node);
  assign {pull_resistor_2_node_2, pull_resistor_2_node} = and_6_out ? register_3_q : 16'bz;  // Controlled_Buffer controlled_buffer_4
  Register #(.width(16)) register_3 (
    .D({pull_resistor_2_node_2, pull_resistor_2_node}), .Q(register_3_q), .clk(and_11_out), .clr(Reset));  // open: en
  and and_11 (and_11_out, comparator_6_eq, pull_resistor_3_node, pull_resistor_4_node);
  assign {pull_resistor_2_node_2, pull_resistor_2_node} = and_7_out ? register_4_q : 16'bz;  // Controlled_Buffer controlled_buffer_5
  Register #(.width(16)) register_4 (
    .D({pull_resistor_2_node_2, pull_resistor_2_node}), .Q(register_4_q), .clk(and_12_out), .clr(Reset));  // open: en
  and and_12 (and_12_out, comparator_7_eq, pull_resistor_3_node, pull_resistor_4_node);
  Hex_Digit_Display hex_digit_display_4 (.value(StatusLCD[3:0]));  // open: dp
  assign {pull_resistor_1_node_2, pull_resistor_1_node} = DMA ? adder_1_out : 16'bz;  // Controlled_Buffer controlled_buffer_6
  assign {pull_resistor_2_node_2, pull_resistor_2_node} = DMA ? rom_2_data : 16'bz;  // Controlled_Buffer controlled_buffer_7
  assign pull_resistor_3_node = DMA ? 1'b1 : 1'bz;  // Controlled_Buffer controlled_buffer_8
  assign pull_resistor_4_node = DMA ? t_ff_1_q : 1'bz;  // Controlled_Buffer controlled_buffer_9
  ROM #(.dataWidth(16)) rom_1 (.addr(pull_resistor_1_node), .data(rom_1_data));
  J_K_Flip_Flop j_k_ff_1 (
    .J(or_1_out), .clk(or_2_out), .K(comparator_8_eq), .Q(DMA), .Qn(j_k_ff_1_qn), .reset(Reset));  // open: preset
  or or_2 (or_2_out, or_1_out, comparator_8_eq);
  Counter #(.max('hffff), .width(16)) counter_1 (
    .Q(counter_1_q), .clk(t_ff_1_qn), .clr(j_k_ff_1_qn));  // open: load, D, count, carry, up
  Adder #(.width(16)) adder_1 (.a(register_1_q), .b(counter_1_q), .out(adder_1_out));  // open: cin, cout
  assign bit_extender_1_out = {{8{counter_1_q[15]}}, counter_1_q};  // Bit_Extender bit_extender_1
  Adder #(.width(24)) adder_2 (
    .a(bit_extender_1_out), .b({register_4_q[7:0], register_3_q}), .out(adder_2_out));  // open: cin, cout
  and and_13 (and_13_out, d_ff_1_qn, DMA);
  not not_1 (not_1_out, pull_resistor_1_node_2[15]);
  T_Flip_Flop t_ff_1 (.clk(CLK), .T(DMA), .Q(t_ff_1_q), .Qn(t_ff_1_qn), .reset(Reset));  // open: preset
  Comparator #(.width(16)) comparator_8 (.a(register_2_q), .b(counter_1_q), .eq(comparator_8_eq));  // open: gt, lt
  D_Flip_Flop d_ff_1 (.clk(and_13_out), .D(and_13_out), .Qn(d_ff_1_qn), .reset(Reset));  // open: Q, preset
  not not_2 (not_2_out, pull_resistor_3_node);
  and and_14 (and_14_out, and_15_out, pull_resistor_4_node);
  and and_15 (and_15_out, not_1_out, ~d_ff_1_qn);  // AND_Gate
  assign controlled_buffer_10_out = pull_resistor_3_node ? {pull_resistor_2_node_2, pull_resistor_2_node} : 16'bz;  // Controlled_Buffer controlled_buffer_10
  and and_16 (and_16_out, and_15_out, ~pull_resistor_3_node);  // AND_Gate
  assign {pull_resistor_2_node_2, pull_resistor_2_node} = and_16_out ? controlled_buffer_10_out : 16'bz;  // Controlled_Buffer controlled_buffer_11
  assign {pull_resistor_2_node_2, pull_resistor_2_node} = and_17_out ? rom_1_data : 16'bz;  // Controlled_Buffer controlled_buffer_12
  ROM #(.addrWidth(24), .dataWidth(16)) rom_2 (.addr(adder_2_out), .data(rom_2_data));
  RAM #(.addrWidth(16), .asyncread("true"), .clearpin("true"), .dataWidth(16), .databus("bidir")) ram_1 (
    .addr({pull_resistor_1_node_2, pull_resistor_1_node}), .we(and_15_out), .oe(not_2_out), .clk(and_14_out),
    .data(controlled_buffer_10_out), .clr(Reset));
  and and_17 (and_17_out, not_1_out, d_ff_1_qn, not_2_out);
  and and_18 (and_18_out, comparator_9_eq, pull_resistor_3_node, pull_resistor_4_node);
  Comparator #(.mode("unsigned"), .width(16)) comparator_9 (
    .a(16'hfffe), .b({pull_resistor_1_node_2, pull_resistor_1_node}), .eq(comparator_9_eq));  // open: gt, lt
  Register #(.width(16)) register_5 (
    .D({pull_resistor_2_node_2, pull_resistor_2_node}), .Q(register_5_q), .clk(and_18_out), .clr(Reset));  // open: en
  and and_19 (and_19_out, comparator_9_eq, ~pull_resistor_3_node);  // AND_Gate
  assign {pull_resistor_2_node_2, pull_resistor_2_node} = and_19_out ? register_5_q : 16'bz;  // Controlled_Buffer controlled_buffer_13
  Register #(.width(16)) register_6 (
    .D({pull_resistor_2_node_2, pull_resistor_2_node}), .Q(register_6_q), .clk(and_20_out), .clr(Reset));  // open: en
  and and_20 (and_20_out, comparator_10_eq, pull_resistor_3_node, pull_resistor_4_node);
  Comparator #(.mode("unsigned"), .width(16)) comparator_10 (
    .a(16'hfff1), .b({pull_resistor_1_node_2, pull_resistor_1_node}), .eq(comparator_10_eq));  // open: gt, lt
  and and_21 (and_21_out, comparator_10_eq, ~pull_resistor_3_node);  // AND_Gate
  assign {pull_resistor_2_node_2, pull_resistor_2_node} = and_21_out ? register_6_q : 16'bz;  // Controlled_Buffer controlled_buffer_14
  Register #(.width(16)) register_7 (
    .D({pull_resistor_2_node_2, pull_resistor_2_node}), .Q(register_7_q), .clk(and_22_out), .clr(Reset));  // open: en
  and and_22 (and_22_out, comparator_11_eq, pull_resistor_3_node, pull_resistor_4_node);
  Comparator #(.mode("unsigned"), .width(16)) comparator_11 (
    .a(16'hfff0), .b({pull_resistor_1_node_2, pull_resistor_1_node}), .eq(comparator_11_eq));  // open: gt, lt
  not not_3 (not_3_out, DMA);
  and and_23 (and_23_out, not_3_out, nand_1_out);
  and and_24 (and_24_out, comparator_11_eq, ~pull_resistor_3_node);  // AND_Gate
  assign {pull_resistor_2_node_2, pull_resistor_2_node} = and_24_out ? register_7_q : 16'bz;  // Controlled_Buffer controlled_buffer_15
  assign controlled_buffer_16_out = not_4_out ? Data : 16'bz;  // Controlled_Buffer controlled_buffer_16
  assign {pull_resistor_2_node_2, pull_resistor_2_node} = controlled_buffer_16_out;  // OR_Gate or_3, 16 bits wide OR_Gate
  nand nand_1 (nand_1_out, multiplexer_2_out, ~or_7_out);  // NAND_Gate
  and and_25 (and_25_out, DMA, nand_1_out);
  assign {pull_resistor_1_node_2, pull_resistor_1_node} = and_23_out ? multiplexer_1_out : 16'bz;  // Controlled_Buffer controlled_buffer_17
  assign Adress = and_25_out ? {pull_resistor_1_node_2, pull_resistor_1_node} : 16'bz;  // Controlled_Buffer controlled_buffer_18
  assign pull_resistor_3_node = and_23_out ? ReadWrite : 1'bz;  // Controlled_Buffer controlled_buffer_19
  assign ReadWrite = and_25_out ? pull_resistor_3_node : 1'bz;  // Controlled_Buffer controlled_buffer_20
  assign pull_resistor_4_node = and_23_out ? Strobe : 1'bz;  // Controlled_Buffer controlled_buffer_21
  assign Strobe = and_25_out ? pull_resistor_4_node : 1'bz;  // Controlled_Buffer controlled_buffer_22
  not not_4 (not_4_out, or_5_out);
  assign Data = controlled_buffer_23_out;  // OR_Gate or_4, 16 bits wide OR_Gate
  assign controlled_buffer_23_out = or_5_out ? {pull_resistor_2_node_2, pull_resistor_2_node} : 16'bz;  // Controlled_Buffer controlled_buffer_23
  not not_5 (not_5_out, multiplexer_2_out);
  Adder #(.width(16)) adder_3 (.a(register_7_q), .b(Adress), .out(adder_3_out));  // open: cin, cout
  Multiplexer #(.width(16)) multiplexer_1 (.in0(adder_3_out), .in1(Adress), .out(multiplexer_1_out));  // open: sel
  or or_5 (or_5_out, DMA, not_6_out);
  not not_6 (not_6_out, or_6_out);
  Demultiplexer demultiplexer_1 (
    .out0(demultiplexer_1_out0), .out1(demultiplexer_1_out1), .in(and_26_out), .sel(InInt));
  or or_6 (or_6_out, ReadWrite, or_8_out);
  T_Flip_Flop t_ff_2 (.clk(demultiplexer_1_out0), .T(1'b1), .Q(t_ff_2_q), .reset(Reset));  // open: Qn, preset
  Multiplexer multiplexer_2 (.in0(t_ff_2_q), .in1(t_ff_3_q), .out(multiplexer_2_out));  // open: sel
  T_Flip_Flop t_ff_3 (.clk(demultiplexer_1_out1), .T(1'b1), .Q(t_ff_3_q), .reset(Reset));  // open: Qn, preset
  or or_7 (or_7_out, comparator_12_gt, comparator_12_eq);
  Comparator #(.mode("unsigned"), .width(16)) comparator_12 (
    .a(register_6_q), .b(multiplexer_1_out), .gt(comparator_12_gt), .eq(comparator_12_eq));  // open: lt
  Comparator #(.mode("unsigned"), .width(16)) comparator_13 (
    .a({16{1'b1}}), .b(Adress), .eq(comparator_13_eq));  // open: gt, lt
  Comparator #(.mode("unsigned"), .width(16)) comparator_14 (
    .a({16{1'b0}}), .b(Data), .eq(comparator_14_eq));  // open: gt, lt
  and and_26 (and_26_out, comparator_13_eq, ReadWrite, Strobe, ~DMA, comparator_14_eq);  // AND_Gate
  Pull_Resistor pull_resistor_10 (.node(Adress));
  Pull_Resistor pull_resistor_11 (.node(Data));
  or or_8 (or_8_out, or_11_out, or_9_out);
  Pull_Resistor pull_resistor_12 (.node(ReadWrite));
  Pull_Resistor pull_resistor_13 (.node(Strobe));
  Pull_Resistor pull_resistor_14 (.node(Reset));
  Pull_Resistor pull_resistor_15 (.node(Interrupt));
  Pull_Resistor pull_resistor_16 (.node(DMA));
  Pull_Resistor pull_resistor_17 (.node(CLK));
  Pull_Resistor pull_resistor_18 (.node(InInt));
  Register #(.width(16)) register_8 (.D(Data), .Q(register_8_q), .clk(and_27_out), .clr(Reset));  // open: en
  and and_27 (and_27_out, comparator_15_eq, ReadWrite, Strobe);
  Comparator #(.mode("unsigned"), .width(16)) comparator_15 (
    .a(16'hfffa), .b(Adress), .eq(comparator_15_eq));  // open: gt, lt
  or or_9 (or_9_out, and_28_out, or_10_out);
  and and_28 (and_28_out, comparator_15_eq, ~ReadWrite);  // AND_Gate
  assign Data = and_28_out ? register_8_q : 16'bz;  // Controlled_Buffer controlled_buffer_24
  Register #(.width(16)) register_9 (.D(Data), .Q(register_9_q), .clk(and_29_out), .clr(Reset));  // open: en
  and and_29 (and_29_out, comparator_16_eq, ReadWrite, Strobe);
  Comparator #(.mode("unsigned"), .width(16)) comparator_16 (
    .a(16'hfffb), .b(Adress), .eq(comparator_16_eq));  // open: gt, lt
  or or_10 (or_10_out, and_30_out, or_12_out);
  Negator #(.width(16)) negator_1 (.in(register_9_q), .out(negator_1_out));
  and and_30 (and_30_out, comparator_16_eq, ~ReadWrite);  // AND_Gate
  assign Data = and_30_out ? register_9_q : 16'bz;  // Controlled_Buffer controlled_buffer_25
  or or_11 (or_11_out, and_35_out, and_37_out);
  not not_7 (not_7_out, register_8_q[3]);
  Multiplexer #(.width(16)) multiplexer_3 (
    .in0(negator_1_out), .in1(register_9_q), .out(multiplexer_3_out), .sel(not_7_out));
  and and_31 (and_31_out, comparator_17_eq, ReadWrite, Strobe);
  Comparator #(.mode("unsigned"), .width(16)) comparator_17 (
    .a(16'hfffc), .b(Adress), .eq(comparator_17_eq));  // open: gt, lt
  Register #(.width(16)) register_10 (.D(Data), .Q(register_10_q), .clk(and_31_out), .clr(Reset));  // open: en
  and and_32 (and_32_out, comparator_17_eq, ~ReadWrite);  // AND_Gate
  assign Data = and_32_out ? register_10_q : 16'bz;  // Controlled_Buffer controlled_buffer_26
  or or_12 (or_12_out, and_32_out, and_34_out);
  Comparator #(.mode("unsigned"), .width(16)) comparator_18 (
    .a(16'hfff9), .b(Adress), .eq(comparator_18_eq));  // open: gt, lt
  not not_8 (not_8_out, register_8_q[5]);
  Negator #(.width(16)) negator_2 (.in(register_10_q), .out(negator_2_out));
  Multiplexer #(.width(16)) multiplexer_4 (
    .in0(negator_2_out), .in1(register_10_q), .out(multiplexer_4_out), .sel(not_8_out));
  Comparator #(.mode("unsigned"), .width(16)) comparator_19 (
    .a(16'hfffd), .b(Adress), .eq(comparator_19_eq));  // open: gt, lt
  Register #(.width(16)) register_11 (.D(Data), .Q(StatusLCD), .clk(and_33_out), .clr(Reset));  // open: en
  and and_33 (and_33_out, comparator_18_eq, ReadWrite, Strobe);
  and and_34 (and_34_out, comparator_19_eq, ~ReadWrite);  // AND_Gate
  assign Data = and_34_out ? multiplexer_5_out : 16'bz;  // Controlled_Buffer controlled_buffer_27
  and and_35 (and_35_out, comparator_18_eq, ~ReadWrite);  // AND_Gate
  assign Data = and_35_out ? StatusLCD : 16'bz;  // Controlled_Buffer controlled_buffer_28
  Comparator #(.width(16)) comparator_20 (
    .a(multiplexer_3_out), .b(multiplexer_4_out), .gt(comparator_20_gt), .eq(comparator_20_eq),
    .lt(comparator_20_lt));
  Comparator #(.mode("unsigned"), .width(16)) comparator_21 (
    .a(Adress), .b({16{1'b1}}), .eq(comparator_21_eq));  // open: gt, lt
  Adder #(.width(16)) adder_4 (.a(multiplexer_3_out), .b(multiplexer_4_out), .out(adder_4_out));  // open: cin, cout
  assign bit_extender_2_out = {{15{1'b0}}, comparator_20_gt};  // Bit_Extender bit_extender_2
  assign bit_extender_3_out = {{15{1'b0}}, comparator_20_eq};  // Bit_Extender bit_extender_3
  assign bit_extender_4_out = {{15{1'b0}}, comparator_20_lt};  // Bit_Extender bit_extender_4
  assign and_36_out = multiplexer_3_out & multiplexer_4_out;  // AND_Gate and_36, 16 bits wide
  assign or_13_out = multiplexer_3_out | multiplexer_4_out;  // OR_Gate or_13, 16 bits wide
  assign not_9_out = ~multiplexer_3_out;  // NOT_Gate not_9, 16 bits wide
  Adder #(.width(16)) adder_5 (.a(not_10_out), .b(Data), .out(adder_5_out), .cin(1'b1));  // open: cout
  Demultiplexer demultiplexer_2 (
    .out0(demultiplexer_2_out0), .out1(demultiplexer_2_out1), .in(or_15_out), .sel(d_ff_2_q));
  and and_37 (and_37_out, ~ReadWrite, comparator_21_eq);  // AND_Gate
  and and_38 (and_38_out, comparator_21_eq, ReadWrite);
  Multiplexer #(.select(3), .width(16)) multiplexer_5 (
    .in0(adder_4_out), .in1(bit_extender_2_out), .in2(bit_extender_3_out), .in3(bit_extender_4_out),
    .in4(and_36_out), .in5(or_13_out), .in6(not_9_out), .in7(undriven), .out(multiplexer_5_out),
    .sel(register_8_q[2:0]));
  assign not_10_out = ~register_5_q;  // NOT_Gate not_10, 16 bits wide
  Counter #(.max('hffff), .width(16)) counter_2 (
    .load(and_38_out), .D(adder_5_out), .count(not_11_out), .Q(counter_2_q), .clk(demultiplexer_2_out1),
    .clr(or_14_out));  // open: carry, up
  or or_14 (or_14_out, ~d_ff_2_q, Reset);  // OR_Gate
  Counter #(.max('hffff), .width(16)) counter_3 (
    .load(and_38_out), .D(Data), .count(not_11_out), .Q(counter_3_q), .clk(demultiplexer_2_out0), .clr(Reset));  // open: carry, up
  assign Data = and_37_out ? multiplexer_6_out : 16'bz;  // Controlled_Buffer controlled_buffer_29
  not not_11 (not_11_out, and_38_out);
  or or_15 (or_15_out, and_39_out, and_40_out);
  and and_39 (and_39_out, and_38_out, Strobe);
  Comparator #(.mode("unsigned"), .width(16)) comparator_22 (
    .a({16{1'b0}}), .b(register_5_q), .eq(comparator_22_eq));  // open: gt, lt
  Adder #(.width(16)) adder_6 (.a(register_5_q), .b(counter_2_q), .out(adder_6_out));  // open: cin, cout
  Multiplexer #(.width(16)) multiplexer_6 (
    .in0(counter_3_q), .in1(adder_6_out), .out(multiplexer_6_out), .sel(d_ff_2_q));
  and and_40 (and_40_out, or_25_out, CPUclk);
  assign Adress = not_12_out ? register_12_q : 16'bz;  // Controlled_Buffer controlled_buffer_30
  assign ReadWrite = not_12_out ? and_51_out : 1'bz;  // Controlled_Buffer controlled_buffer_31
  not not_12 (not_12_out, DMA);
  assign InInt = not_12_out ? d_ff_2_q : 1'bz;  // Controlled_Buffer controlled_buffer_32
  assign controlled_buffer_33_out = or_22_out ? multiplexer_6_out : 16'bz;  // Controlled_Buffer controlled_buffer_33
  assign Strobe = not_12_out ? and_42_out : 1'bz;  // Controlled_Buffer controlled_buffer_34
  assign controlled_buffer_33_out = or_24_out ? Data : 16'bz;  // Controlled_Buffer controlled_buffer_35
  Clock clock_1 (.out(CLK));
  assign Data = and_41_out ? controlled_buffer_33_out : 16'bz;  // Controlled_Buffer controlled_buffer_36
  and and_41 (and_41_out, not_12_out, and_51_out);
  and and_42 (and_42_out, and_51_out, CPUclk);
  or or_16 (or_16_out, not_12_out, CPUclk);
  T_Flip_Flop t_ff_4 (.clk(CLK), .T(or_16_out), .Q(CPUclk), .reset(Reset));  // open: Qn, preset
  and and_43 (and_43_out, or_23_out, CPUclk);
  Register #(.width(16)) register_12 (
    .D(controlled_buffer_33_out), .Q(register_12_q), .clk(and_43_out), .clr(Reset));  // open: en
  Register #(.width(16)) register_13 (
    .D(controlled_buffer_33_out), .Q(register_13_q), .clk(and_44_out), .clr(Reset));  // open: en
  and and_44 (and_44_out, and_47_out, CPUclk);
  Counter #(.max('h7), .width(3)) counter_4 (
    .Q(CPUstep), .clk(not_13_out), .clr(or_17_out));  // open: load, D, count, carry, up
  or or_17 (or_17_out, and_53_out, Reset);
  not not_13 (not_13_out, CPUclk);
  assign controlled_buffer_33_out = and_51_out ? register_13_q : 16'bz;  // Controlled_Buffer controlled_buffer_37
  and and_45 (and_45_out, ~CPUstep[0], ~CPUstep[1], ~CPUstep[2]);  // AND_Gate
  or or_18 (Reset, por_1_out, button_1_out);
  POR por_1 (.out(por_1_out));
  Button button_1 (.out(button_1_out));
  and and_46 (and_46_out, CPUstep[0], ~CPUstep[1], ~CPUstep[2]);  // AND_Gate
  or or_19 (or_19_out, and_46_out, and_45_out);
  or or_20 (or_20_out, and_47_out, and_46_out);
  and and_47 (and_47_out, ~CPUstep[0], CPUstep[1], ~CPUstep[2]);  // AND_Gate
  and and_48 (and_48_out, ~comparator_22_eq, and_52_out, CPUclk);  // AND_Gate
  or or_21 (or_21_out, and_49_out, or_19_out);
  or or_22 (or_22_out, and_49_out, and_45_out);
  and and_49 (and_49_out, CPUstep[0], CPUstep[1], ~CPUstep[2]);  // AND_Gate
  and and_50 (and_50_out, ~CPUstep[0], ~CPUstep[1], CPUstep[2]);  // AND_Gate
  D_Flip_Flop d_ff_2 (.clk(and_48_out), .D(Interrupt), .Q(d_ff_2_q), .reset(Reset));  // open: Qn, preset
  or or_23 (or_23_out, and_50_out, or_21_out);
  or or_24 (or_24_out, and_50_out, or_20_out);
  or or_25 (or_25_out, and_50_out, and_46_out);
  and and_51 (and_51_out, CPUstep[0], ~CPUstep[1], CPUstep[2]);  // AND_Gate
  and and_52 (and_52_out, ~CPUstep[0], CPUstep[1], CPUstep[2]);  // AND_Gate
  and and_53 (and_53_out, CPUstep[0], CPUstep[1], CPUstep[2]);

  // Notes on the sheet:
  //   0-Uninitialized
  //   1-Working
  //   2-Idle
  //   3-Loading Program
  //   4-Loading Data
  //   5-Halted
  //   Write
  //   Start
  //   Trans
  //   Length
  //   Read
  //   Low
  //   Read
  //   High
  //   contents of rom_1 (hex, n*v repeats v):
  //   48 ffff 36 fff2 37 fff9 36 fff6 36 fff5 47 fff4 36 fff3 3c fff8 45 fff8 3d fff8 3e fff8 41 fff8 44
  //   fff8 40 fff8 3a fff8 42 fff8 3f fff8 46 fff8 44 fff8 3f fff8 43 fff8 3b fff8 3b fff8 3b fff8 39 fff8
  //   38 fff9 49 ffff 0 1 3 a 20 2e 4c 61 64 65 67 69 6b 6c 6e 6f 72 700 6 2
  //   contents of rom_2 (hex, n*v repeats v):
  //   646 ffff 0 0 63b fff9 647 648 649 64a 64b 64c 64d 64e 64f 650 648 651 648 652 64a 653 64c 654 64e
  //   655 650 656 647 657 658 659 656 23 644 0 65a 65b 643 fffa 65c fffb 63b fffc fffd 35 63a fffa 63f
  //   fffc ffff fffb fffd 0 65c ffff 65d 65e 643 fffa 65f fffb 63b fffc fffd 49 63a fffa 63f fffc ffff
  //   fffb fffd 0 65f ffff 660 661 659 662 643 fffa 663 fffb 63b fffc fffd 5f 63a fffa 63f fffc ffff fffb
  //   fffd 0 663 ffff 664 fffe 659 fffc 665 fffb 643 fffa 659 666 659 fff0 fffd fff1 63a ffff fffb 667
  //   fffc 668 63a 669 66a 89 66b fffb 63a fffa 63f fffc fffd fffb ffff fffc fffd 86 0 ffff 8a 0 66c ffff
  //   666 fffb 63c fffc 63a fffa fffd 94 0 66d fffd 99 66e 0 63b 669 63a 66b 63a 66f 667 fffb 63a fffc 63c
  //   fffa fffd 670 671 b9 670 fffb 63a fffa 63f fffc fffd fffb ffff fffc fffd b6 0 ffff ba 0 667 fffb 63b
  //   fffc 63c fffa fffd 670 672 d3 670 fffb 63a fffa 63f fffc fffd fffb ffff fffc fffd d0 0 ffff d4 0 667
  //   fffb 63c fffc 63c fffa fffd 670 673 ed 670 fffb 63a fffa 63f fffc fffd fffb ffff fffc fffd ea 0 ffff
  //   ee 0 667 fffb 63d fffc 63c fffa fffd 670 674 107 670 fffb 63a fffa 63f fffc fffd fffb ffff fffc fffd
  //   104 0 ffff 108 0 667 fffb 63e fffc 63c fffa fffd 670 675 121 670 fffb 63a fffa 63f fffc fffd fffb
  //   ffff fffc fffd 11e 0 ffff 122 0 667 fffb 63f fffc 63c fffa fffd 670 676 13b 670 fffb 63a fffa 63f
  //   fffc fffd fffb ffff fffc fffd 138 0 ffff 13c 0 667 fffb 640 fffc 63c fffa fffd 670 677 155 670 fffb
  //   63a fffa 63f fffc fffd fffb ffff fffc fffd 152 0 ffff 156 0 667 fffb 641 fffc 63c fffa fffd 670 678
  //   16f 670 fffb 63a fffa 63f fffc fffd fffb ffff fffc fffd 16c 0 ffff 170 0 667 fffb 642 fffc 63c fffa
  //   fffd 670 679 189 670 fffb 63a fffa 63f fffc fffd fffb ffff fffc fffd 186 0 ffff 18a 0 67a ffff 668
  //   fff8 67b ffff 63a fff7 67b ffff fff7 66f 67b ffff 668 fffb 666 fffc 63a fffa fffd 67c 67c 1a2 0 67d
  //   67d fffb 666 fffc 63a fffa fffd 67d 63a fffa 63b fffc 67c fffb fffd 67c 67c 1b6 0 67e 67e fffb 666
  //   fffc 63a fffa fffd 67e 67e 67f 655 680 643 fffa 681 fffb 63b fffc fffd 1d3 63a fffa 63f fffc ffff
  //   fffb fffd 0 681 ffff 67d 65e 643 fffa 65f fffb 63b fffc fffd 1e7 63a fffa 63f fffc ffff fffb fffd 0
  //   65f ffff 660 661 659 662 643 fffa 663 fffb 63b fffc fffd 1fd 63a fffa 63f fffc ffff fffb fffd 0 663
  //   ffff 659 fffc 665 fffb 643 fffa 659 666 659 fff0 fffd fff1 63a ffff 67b ffff 668 fffb 666 fffc 63a
  //   fffa fffd 668 655 67f 668 680 643 fffa 681 fffb 63b fffc fffd 22b 63a fffa 63f fffc ffff fffb fffd 0
  //   681 ffff 67b ffff 668 fffb 666 fffc 63a fffa fffd 668 656 67f 668 680 643 fffa 681 fffb 63b fffc
  //   fffd 24b 63a fffa 63f fffc ffff fffb fffd 0 681 ffff 67b ffff 668 fffb 666 fffc 63a fffa fffd 668
  //   668 67f 656 680 643 fffa 681 fffb 63b fffc fffd 26b 63a fffa 63f fffc ffff fffb fffd 0 681 ffff 67b
  //   ffff 668 fffb 666 fffc 63a fffa fffd 682 682 27a 0 683 63a fffa 63b fffc 682 fffb fffd 682 682 286 0
  //   fffb 666 fffc 63a fffa fffd 684 63a fff6 683 fff5 645 fff4 684 fff3 63e fff9 63a fff2 63b fff9 67b
  //   ffff 668 fffb 666 fffc 63a fffa fffd 65e 643 fffa 65f fffb 63b fffc fffd 2b5 63a fffa 63f fffc ffff
  //   fffb fffd 0 65f ffff 660 66f 67b ffff 666 fffb 63e fffc 63a fffa fffd 2c5 66f 0 685 2d7 669 fffb 63a
  //   fffa 63f fffc fffd fffb ffff fffc fffd 2d4 0 ffff 2d8 0 686 ffff 666 fffb 63c fffc 63a fffa fffd 2e3
  //   66d 0 63a 669 63b 66b 666 fffc 665 fffb 643 fffa 666 666 666 fff0 fffd fff1 63a ffff 687 fff9 fff8 0
  //   67a ffff 63b 66b 666 fffb 63c fffc 63a fffa fffd 306 0 66e fffd 30b 63e 0 666 fffc 665 fffb 643 fffa
  //   666 666 666 fff0 fffd fff1 63a ffff 0 0 67f 31e 0 689 680 323 689 0 63a fffa 63b fffc 67f fffb fffd
  //   67f 63a fffa 63b fffc 680 fffb fffd 680 689 fffb 63a fffc 63c fffa 68a 34b fffd fffb 63a fffa 63f
  //   fffc fffd fffb ffff fffc fffd 348 0 ffff 34c 0 688 ffff 643 fffa 681 fffb 63b fffc fffd 356 0 ffff 0
  //   0 65b 35c 0 68c 68c fffb 63a fffc 63c fffa 68d 375 fffd fffb 63a fffa 63f fffc fffd fffb ffff fffc
  //   fffd 372 0 ffff 376 0 68c fff8 63a fffa 63b fffc 65b fffb fffd 65b 68b ffff 643 fffa 65c fffb 63b
  //   fffc fffd 38a 0 ffff 0 0 63a 68e 63a fff6 661 fff5 652 fff3 645 fff4 fff9 68f 63e fff9 0 fff2 68f
  //   fff9 652 690 63a fffa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
  //   or_3 drives only 1 and floats otherwise
  //   or_4 drives only 1 and floats otherwise
endmodule
